# Fritzing sketch motherboard (saved by Fritzing 0.9.2b)
circuit board: 10cm x 10cm
breadboards: 1

parts:
  VOUT+ = male pin header, 5 pins [form="♂ (male)"]
  VOUT- = male pin header, 5 pins [form="♂ (male)"]
  D3 = Rectifier Diode [part_number=1N4001 package="300 mil [THT]"]
  WALL = male pin header, 2 pins [form="♂ (male)"]
  BATT = male pin header, 2 pins [form="♂ (male)"]
  D1 = Rectifier Diode [part_number=1N4001 package="300 mil [THT]"]
  D2 = Rectifier Diode [part_number=1N4001 package="300 mil [THT]"]
  SWITCH_IN = mystery part, 2 pins [chip_label=?]
  SWITCH_OUT = mystery part, 4 pins [chip_label=?]
  FL-C = Electrolytic Capacitor [capacitance=1µF package="100 mil [THT, electrolytic]"]
  BL-C = Electrolytic Capacitor [capacitance=1µF package="100 mil [THT, electrolytic]"]
  FR-C = Electrolytic Capacitor [capacitance=1µF package="100 mil [THT, electrolytic]"]
  BR-C = Electrolytic Capacitor [capacitance=1µF package="100 mil [THT, electrolytic]"]
  BL_MOTOR = male pin header, 4 pins [form="♂ (male)"]  # not connected
  FL_MOTOR = male pin header, 4 pins [form="♂ (male)"]  # not connected
  BR_MOTOR = male pin header, 4 pins [form="♂ (male)"]  # not connected
  FR_MOTOR = male pin header, 4 pins [form="♂ (male)"]  # not connected
  5V-I2C = male pin header, 2 pins [form="♂ (male)"]
  FL_DRIVER = mystery part, 16 pins [chip_label=?]
  BL_DRIVER = mystery part, 16 pins [chip_label=?]
  BR_DRIVER = mystery part, 16 pins [chip_label=?]
  MOTOR_PWR = male pin header, 2 pins [form="♂ (male)"]
  ARDUINO_PWR = male pin header, 2 pins [form="♂ (male)"]
  5V+ = male pin header, 6 pins [form="♂ (male)"]
  5V- = male pin header, 6 pins [form="♂ (male)"]
  3V+ = male pin header, 6 pins [form="♂ (male)"]
  3V- = male pin header, 6 pins [form="♂ (male)"]
  FR_DRIVER = mystery part, 16 pins [chip_label=?]
  AIN0 = male pin header, 3 pins [form="♂ (male)"]
  AIN1 = male pin header, 3 pins [form="♂ (male)"]
  AIN2 = male pin header, 3 pins [form="♂ (male)"]
  AIN3 = male pin header, 3 pins [form="♂ (male)"]
  AIN4 = male pin header, 3 pins [form="♂ (male)"]
  AIN5 = male pin header, 3 pins [form="♂ (male)"]
  ARDUINO = mystery part, 34 pins [chip_label=?]
  5V-C1 = Electrolytic Capacitor [capacitance=1µF package="100 mil [THT, electrolytic]"]
  5V-C2 = Electrolytic Capacitor [capacitance=1µF package="100 mil [THT, electrolytic]"]
  3V-C3 = Electrolytic Capacitor [capacitance=1µF package="100 mil [THT, electrolytic]"]

nets:
  N1: VOUT+.pin1, VOUT+.pin2, VOUT+.pin3, VOUT+.pin4, VOUT+.pin5, D1.cathode, D2.cathode
  N2: VOUT-.pin1, VOUT-.pin2, VOUT-.pin3, VOUT-.pin4, VOUT-.pin5, D3.anode
  N3: D3.cathode, WALL.pin2, BATT.pin2
  N4: WALL.pin1, SWITCH_IN.pin1
  N5: BATT.pin1, SWITCH_IN.pin2, SWITCH_OUT.pin1
  N6: D1.anode, SWITCH_OUT.pin4
  N7: D2.anode, SWITCH_OUT.pin2
  N8: FL-C.-, BL-C.-, FR-C.-, BR-C.-, FL_DRIVER.pin7, BL_DRIVER.pin7, BR_DRIVER.pin7, MOTOR_PWR.pin1, FR_DRIVER.pin7
  N9: FL-C.+, BL-C.+, FR-C.+, BR-C.+, FL_DRIVER.pin8, BL_DRIVER.pin8, BR_DRIVER.pin8, MOTOR_PWR.pin2, FR_DRIVER.pin8
  N10: 5V-I2C.pin1, ARDUINO.pin25
  N11: 5V-I2C.pin2, ARDUINO.pin24
  N12: FL_DRIVER.pin1, BL_DRIVER.pin1, BR_DRIVER.pin1, ARDUINO_PWR.pin1, 5V-.pin1, 5V-.pin2, 5V-.pin3, 5V-.pin4, 5V-.pin5, 5V-.pin6, 3V-.pin1, 3V-.pin2, 3V-.pin3, 3V-.pin4, 3V-.pin5, 3V-.pin6, FR_DRIVER.pin1, AIN0.pin3, AIN1.pin3, AIN2.pin3, AIN3.pin3, AIN4.pin3, AIN5.pin3, ARDUINO.pin14, ARDUINO.pin23, 5V-C1.-, 5V-C2.-, 3V-C3.-
  N13: FL_DRIVER.pin2, BL_DRIVER.pin2, BR_DRIVER.pin2, 5V+.pin1, 5V+.pin2, 5V+.pin3, 5V+.pin4, 5V+.pin5, 5V+.pin6, FR_DRIVER.pin2, AIN0.pin2, AIN1.pin2, AIN2.pin2, AIN3.pin2, AIN4.pin2, AIN5.pin2, ARDUINO.pin12, 5V-C1.+, 5V-C2.+
  N14: ARDUINO_PWR.pin2, ARDUINO.pin15
  N15: 3V+.pin1, 3V+.pin2, 3V+.pin3, 3V+.pin4, 3V+.pin5, 3V+.pin6, ARDUINO.pin2, 3V-C3.+
  N16: AIN0.pin1, ARDUINO.pin5
  N17: AIN1.pin1, ARDUINO.pin6
  N18: AIN2.pin1, ARDUINO.pin7
  N19: AIN4.pin1, ARDUINO.pin8
  N20: AIN5.pin1, ARDUINO.pin9

notes:
  POWER SUPPLY CIRCUIT
